# Fritzing sketch SimpleSpotController (saved by Fritzing 1.0.2b)

parts:
  Part1 = Arduino Uno (Rev3)
  R1 = Rotary Potentiometer (Small) [maximum_resistance=10kΩ knob_status=50% power=0.5W package=THT]
  R2 = Rotary Potentiometer (Small) [maximum_resistance=10kΩ knob_status=50% power=0.5W package=THT]
  U1 = MAX485 [package=dil08]
  XLR2 = XLR3_NCFAH2 [package=xlr3_nc3fah2]

nets:
  N1: Part1.A4/SDA, R2.wiper
  N2: Part1.A5/SCL, R1.wiper
  N3: Part1.D10_PWM/SS, U1.DI
  N4: Part1.5V, R1.leg1, R2.leg1, U1.DE
  N5: Part1.GND, R1.leg2, R2.leg2
  N6: U1.A, XLR2.2
  N7: U1.B, XLR2.3
  N8: XLR2.1, XLR2.G
